// Digital circuit CPU.dig as structural Verilog
module CPU (
  input  [16:0] PRGMR_A,
  input  PRMGR_ACT,
  input  [7:0] PRMR_DATA,
  input  PRMR_WE
);

  wire [7:0] GLS29EE010_70_4C_PHE__EEPROM_d;
  wire [16:0] driverinvsel_1_out, undriven;

  assign driverinvsel_1_out = ~PRMGR_ACT ? undriven : 17'bz;  // DriverInvSel driverinvsel_1
  PullDown pulldown_1 (.out(PRMGR_ACT));
  assign driverinvsel_1_out = PRMGR_ACT ? PRGMR_A : 17'bz;  // Driver driver_1
  PullDown pulldown_2 (.out(PRMR_WE));
  EEPROM #(.AddrBits(17), .Bits(8)) GLS29EE010_70_4C_PHE__EEPROM (
    .A(driverinvsel_1_out), .CS(1'b1), .WE(PRMR_WE), .OE(~PRMGR_ACT), .D(GLS29EE010_70_4C_PHE__EEPROM_d));
  assign GLS29EE010_70_4C_PHE__EEPROM_d = PRMGR_ACT ? PRMR_DATA : 8'bz;  // Driver driver_2
endmodule
